// Logisim project processador_mips.circ as structural Verilog: 1 circuit, main circuit CircuitoMIPS
module CircuitoMIPS (
  input  [3:0] ALUOp,
  input  ALUScr,
  input  MemWrite,
  input  RegWrite,
  input  MemToReg,
  input  MemRead,
  input  RegDst,
  input  Reset,
  input  Branch,
  output [4:0] RegB,
  output [4:0] RegA,
  output [31:0] A,
  output [4:0] RegW,
  output [31:0] B
);

  wire CLK_out, mips_ram_1_p5;
  wire [31:0] adder_1_out, adder_2_out, bit_extender_1_out, mips_alu_1_p4, mips_ram_1_p7,
       mipsprogramrom_1_p3, multiplexer_1_out, PC_q, registerfile_1_p1, registerfile_1_p7, shifter_1_out;

  Clock CLK (.out(CLK_out));
  Register #(.width(32)) PC (.D(multiplexer_1_out), .en(1'b1), .clk(CLK_out), .Q(PC_q), .clr(Reset));
  Adder #(.width(32)) adder_1 (.a(32'h4), .b(PC_q), .out(adder_1_out));  // open: cin, cout
  // MIPSProgramROM mipsprogramrom_1: pin names not known; wires that end beside it: PC_q, CLK_out, {mipsprogramrom_1_p3[31:26], RegA, RegB, mipsprogramrom_1_p3[15:0]}, CLK_out
  assign bit_extender_1_out = {{16{mipsprogramrom_1_p3[15]}}, mipsprogramrom_1_p3[15:0]};  // Bit_Extender bit_extender_1
  Adder #(.width(32)) adder_2 (.a(adder_1_out), .b(shifter_1_out), .out(adder_2_out));  // open: cin, cout
  Multiplexer #(.width(32), .enable("false")) multiplexer_1 (
    .in0(adder_1_out), .in1(adder_2_out), .out(multiplexer_1_out), .sel(Branch));
  Multiplexer #(.width(5), .enable("false")) multiplexer_2 (
    .in0(RegB), .in1(mipsprogramrom_1_p3[15:11]), .out(RegW), .sel(RegDst));
  Shifter #(.width(32)) shifter_1 (.in(bit_extender_1_out), .\dist (5'b00010), .out(shifter_1_out));
  // RegisterFile registerfile_1: pin names not known; wires that end beside it: registerfile_1_p1, RegWrite, RegW, RegA, RegB, A, registerfile_1_p7
  Multiplexer #(.width(32), .enable("false")) multiplexer_3 (
    .in0(registerfile_1_p7), .in1(bit_extender_1_out), .out(B), .sel(ALUScr));
  // Mips_ALU mips_alu_1: pin names not known; wires that end beside it: A, B, ALUOp, mips_alu_1_p4, mips_alu_1_p4[19:0], registerfile_1_p7, MemWrite
  Multiplexer #(.width(32), .enable("false")) multiplexer_4 (
    .in0(mips_alu_1_p4), .in1(mips_ram_1_p7), .out(registerfile_1_p1), .sel(MemToReg));
  // MIPS_RAM mips_ram_1: pin names not known; wires that end beside it: 4'b1111, CLK_out, MemRead, Reset, mips_ram_1_p5, mips_ram_1_p5, mips_ram_1_p7

  // Notes on the sheet:
  //   instruções p/ ALUOp
  //   ---------------------------------
  //   SOMA: 0010
  //   SUBTRAÇÃO: 0110
  //   contents of mipsprogramrom_1 (hex, n*v repeats v):
  //   beq $1, $2, end         lw $5, 0($3)    sw $5, 0($4)    bne $1, $2, loop end:
  //   instruções para o jump:
  //   Branch= 1
  //   ALUop= 0110
  //   RegDst, RegWrite, ALUscr= 0
  //   instruções p/ store(sw- tipo i)
  //   MemWrite, ALUscr= 1
  //   ALUop=0010
  //   instruções p/ load(lw- tipo i)
  //   Branch, RegDst=0
  //   AUop= 0010
  //   RegDst, RegWrite, MemRead, MemToReg= 0
  //   ALUscr, Regwrite,MemRead, MemWrite, MemToReg= 1
endmodule
